# Fritzing sketch circuitDiagram_v1 (saved by Fritzing 0.9.3b)

parts:
  Part1 = Arduino Mega 2560 (Rev3)
  part = TXB0104 4-channel Bi-Directional Level Shifter
  SA686 = IC, SIP package, 10 pins [chip_label=IC]

nets:
  N1: Part1.D11_PWM, part.B1
  N2: Part1.D10_PWM, part.B2
  N3: Part1.3V3, part.LV, SA686.pin2
  GND: Part1.GND, part.GND, SA686.pin1
  N4: Part1.VIN, part.HV
  N5: Part1.D4_PWM, part.B3
  N6: part.A3, SA686.pin10
  N7: part.A2, SA686.pin9
  N8: part.A1, SA686.pin4

notes:
  We use SerialSoftware to reprogram the TX/RX ports. The Arduino Mega only supports SOME of the pins being RX (pin 10 works)
  Remember that the RX of the mega must go into the TX of the SA686 thingy
  YELLOW IS RX OF MEGA
  BLUE IS TX OF MEGA
  Pin labled 5V can also work but I put it to VIN because it's futher from 3V3 to decrease accidental shorting.
  PINS ARE:
  RXD
  TXD
  MIC_IN
  SQ
  AF_OUT
  PTT
  PD
  H/L
  VCC
  GND
  This setup is using an EDITED VERSION of the debug example of the DRA818 library
  (PD is changed to 11, and the RX is changed to 10)

custom parts:
  TXB0104 4-channel Bi-Directional Level Shifter: Because the Arduino (and Basic Stamp) are 5V devices, and most modern sensors, displays, flash cards and modes are 3.3V-only, many makers find that they need to perform level shifting/conversion to protect the 3.3V device from 5V. Although one can use resistors to make a divider, for high speed transfers, the resistors can add a lot of slew and cause havoc that is tough to debug. For that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
